# Fritzing sketch controller-F (saved by Fritzing 0.9.2b)
breadboards: 1

parts:
  LED1 = RGB LED (com. cathode, rgb) [package="5 mm [THT]"]
  p0 = POT [package=alps_pot]
  p1 = POT [package=alps_pot]
  p2 = POT [package=alps_pot]
  p3 = POT [package=alps_pot]
  p4 = POT [package=alps_pot]
  p5 = POT [package=alps_pot]
  Part1 = Arduino Uno (Rev3)
  S4 = Pushbutton [package="[THT]"]
  R2 = Resistor [tolerance=±5% resistance=220 package=THT]
  R3 = Resistor [tolerance=±5% resistance=220 package=THT]
  R4 = Resistor [tolerance=±5% resistance=220 package=THT]

nets:
  N1: LED1.red_anode, R4.Pin_0
  N2: LED1.common_cathode, p0.A, p1.A, p2.A, p3.A, p4.A, p5.A, Part1.5V, S4.Pin_1
  N3: LED1.green_anode, R2.Pin_0
  N4: LED1.blue_anode, R3.Pin_0
  N5: p0.E, p1.E, p2.E, p3.E, p4.E, p5.E, Part1.GND
  N6: p0.S, Part1.A5/SCL
  N7: p1.S, Part1.A4/SDA
  N8: p2.S, Part1.A3
  N9: p3.S, Part1.A2
  N10: p4.S, Part1.A1
  N11: p5.S, Part1.A0
  N12: Part1.D9_PWM, R3.Pin_1
  N13: Part1.D10_PWM/SS, R2.Pin_1
  N14: Part1.D11_PWM/MOSI, R4.Pin_1
  N15: Part1.D13/SCK, S4.Pin_3
